# Fritzing sketch TrafficLight (saved by Fritzing 0.9.3b)
circuit board: 8.46667cm x 5.64444cm
breadboards: 1

parts:
  S1 = Momentary Switch [package=ksa_sealed_tac_switch]
  R1 = Resistor [tolerance=±5% resistance=220 package=THT]
  LED1 = LED - 5mm [color="Green (555nm)" package="5 mm [THT]"]
  LED2 = LED - 5mm [color="Yellow (585nm)" package="5 mm [THT]"]
  LED3 = LED - 5mm [color="Red (633nm)" package="5 mm [THT]"]
  R2 = Resistor [tolerance=±5% resistance=220 package=THT]
  R3 = Resistor [tolerance=±5% resistance=220 package=THT]
  Part1 = Arduino Uno (Rev3)

nets:
  N1: S1.2, Part1.A3
  N2: S1.4, R1.Pin_1, R2.Pin_1, R3.Pin_1, Part1.GND
  N3: R1.Pin_0, LED1.cathode
  N4: LED1.anode, Part1.D7
  N5: LED2.cathode, R2.Pin_0
  N6: LED2.anode, Part1.D8
  N7: LED3.cathode, R3.Pin_0
  N8: LED3.anode, Part1.D9_PWM
